// Logisim project 00-59.circ as structural Verilog: 2 circuits, main circuit main
module main (
  output [3:0] out_1,
  output [3:0] out_2
);

  wire and_1_out, and_2_out, clock_1_out, encoder_7seg_1_out_2, encoder_7seg_1_out_3, encoder_7seg_1_out_4,
       encoder_7seg_1_out_5, encoder_7seg_1_out_6, encoder_7seg_1_out_7, encoder_7seg_1_out_8,
       encoder_7seg_2_out_2, encoder_7seg_2_out_3, encoder_7seg_2_out_4, encoder_7seg_2_out_5,
       encoder_7seg_2_out_6, encoder_7seg_2_out_7, encoder_7seg_2_out_8, or_1_out, or_2_out;

  Clock clock_1 (.out(clock_1_out));
  and and_1 (and_1_out, out_2[1], out_2[3]);
  or or_1 (or_1_out, and_1_out, or_2_out);
  J_K_Flip_Flop #(.trigger("falling")) j_k_ff_1 (
    .J(1'b1), .clk(clock_1_out), .K(1'b1), .Q(out_2[0]), .reset(or_1_out));  // open: Qn, preset, en
  J_K_Flip_Flop #(.trigger("falling")) j_k_ff_2 (
    .J(1'b1), .clk(out_2[0]), .K(1'b1), .Q(out_2[1]), .reset(or_1_out));  // open: Qn, preset, en
  J_K_Flip_Flop #(.trigger("falling")) j_k_ff_3 (
    .J(1'b1), .clk(out_2[1]), .K(1'b1), .Q(out_2[2]), .reset(or_1_out));  // open: Qn, preset, en
  encoder_7seg encoder_7seg_1 (
    .in_1(out_1), .out_2(encoder_7seg_1_out_2), .out_3(encoder_7seg_1_out_3), .out_4(encoder_7seg_1_out_4),
    .out_5(encoder_7seg_1_out_5), .out_6(encoder_7seg_1_out_6), .out_7(encoder_7seg_1_out_7),
    .out_8(encoder_7seg_1_out_8));
  J_K_Flip_Flop #(.trigger("falling")) j_k_ff_4 (
    .J(1'b1), .clk(out_2[2]), .K(1'b1), .Q(out_2[3]), .reset(or_1_out));  // open: Qn, preset, en
  _7_Segment_Display u_7_segment_display_1 (
    .g(encoder_7seg_1_out_8), .f(encoder_7seg_1_out_7), .a(encoder_7seg_1_out_2), .b(encoder_7seg_1_out_3),
    .e(encoder_7seg_1_out_6), .d(encoder_7seg_1_out_5), .c(encoder_7seg_1_out_4));  // open: dp
  encoder_7seg encoder_7seg_2 (
    .in_1(out_2), .out_2(encoder_7seg_2_out_2), .out_3(encoder_7seg_2_out_3), .out_4(encoder_7seg_2_out_4),
    .out_5(encoder_7seg_2_out_5), .out_6(encoder_7seg_2_out_6), .out_7(encoder_7seg_2_out_7),
    .out_8(encoder_7seg_2_out_8));
  or or_2 (or_2_out, and_2_out, out_1[3]);
  J_K_Flip_Flop #(.trigger("falling")) j_k_ff_5 (
    .J(1'b1), .clk(out_2[3]), .K(1'b1), .Q(out_1[0]), .reset(or_2_out));  // open: Qn, preset, en
  and and_2 (and_2_out, out_1[1], out_1[2]);
  _7_Segment_Display u_7_segment_display_2 (
    .g(encoder_7seg_2_out_8), .f(encoder_7seg_2_out_7), .a(encoder_7seg_2_out_2), .b(encoder_7seg_2_out_3),
    .e(encoder_7seg_2_out_6), .d(encoder_7seg_2_out_5), .c(encoder_7seg_2_out_4));  // open: dp
  J_K_Flip_Flop #(.trigger("falling")) j_k_ff_6 (
    .J(1'b1), .clk(out_1[0]), .K(1'b1), .Q(out_1[1]), .reset(or_2_out));  // open: Qn, preset, en
  J_K_Flip_Flop #(.trigger("falling")) j_k_ff_7 (
    .J(1'b1), .clk(out_1[1]), .K(1'b1), .Q(out_1[2]), .reset(or_2_out));  // open: Qn, preset, en
  J_K_Flip_Flop #(.trigger("falling")) j_k_ff_8 (
    .J(1'b1), .clk(out_1[2]), .K(1'b1), .Q(out_1[3]), .reset(or_2_out));  // open: Qn, preset, en
endmodule

module encoder_7seg (
  input  [3:0] in_1,
  output out_2,
  output out_3,
  output out_4,
  output out_5,
  output out_6,
  output out_7,
  output out_8
);

  wire and_1_out, B_prime_C_out, B_prime_D_prime_out, BC_prime_D_out, BC_prime_out, BD_out,
       C_prime_D_prime_out, CD_out, CD_prime_2_out, CD_prime_out, not_1_out, not_2_out, not_3_out, not_4_out;

  not not_1 (not_1_out, in_1[0]);
  not not_2 (not_2_out, in_1[1]);
  not not_3 (not_3_out, in_1[2]);
  not not_4 (not_4_out, in_1[3]);
  and BD (BD_out, in_1[0], in_1[2]);
  and B_prime_D_prime (B_prime_D_prime_out, not_1_out, not_3_out);
  and C_prime_D_prime (C_prime_D_prime_out, not_2_out, not_1_out);
  and CD (CD_out, in_1[1], in_1[0]);
  or or_1 (out_4, in_1[2], not_2_out, in_1[0]);
  and BC_prime_D (BC_prime_D_out, in_1[2], not_2_out, in_1[0]);
  and B_prime_C (B_prime_C_out, not_3_out, in_1[1]);
  and CD_prime (CD_prime_out, in_1[1], not_1_out);
  and BC_prime (BC_prime_out, in_1[2], not_2_out);
  and and_1 (and_1_out, in_1[2], not_1_out);
  or or_2 (out_2, B_prime_D_prime_out, BD_out, in_1[3], in_1[1]);
  or or_3 (out_3, not_3_out, C_prime_D_prime_out, CD_out);
  and CD_prime_2 (CD_prime_2_out, not_1_out, in_1[1]);
  or or_4 (out_6, B_prime_D_prime_out, CD_prime_out);
  or or_5 (out_7, in_1[3], C_prime_D_prime_out, BC_prime_out, and_1_out);
  or or_6 (out_8, BC_prime_out, CD_prime_out, B_prime_C_out, in_1[3]);
  or or_7 (out_5, B_prime_D_prime_out, CD_prime_2_out, BC_prime_D_out, B_prime_C_out, in_1[3]);

  // Notes on the sheet:
  //   D'
  //   C'
  //   B'
  //   A'
endmodule
