// Logisim project CASCADE_UP_DOWN_MOD99.circ as structural Verilog: 3 circuits, main circuit main
module main (
  input  UP_DOWN
);

  wire _7_segment_encoder_2_out_2, _7_segment_encoder_2_out_3, _7_segment_encoder_2_out_4,
       _7_segment_encoder_2_out_5, _7_segment_encoder_2_out_6, _7_segment_encoder_2_out_7,
       _7_segment_encoder_2_out_8, _7_segment_encoder_out_2, _7_segment_encoder_out_3,
       _7_segment_encoder_out_4, _7_segment_encoder_out_5, _7_segment_encoder_out_6,
       _7_segment_encoder_out_7, _7_segment_encoder_out_8, and_1_out, and_2_out, and_3_out, and_4_out,
       CLEAR_out, clock_1_out, not_1_out, not_2_out, not_3_out, not_4_out, not_5_out, not_6_out, not_7_out,
       up_down_1__0, up_down_1__1, up_down_1__2, up_down_1__3, xor_1_out;
  wire [3:0] up_down_1_out_6, up_down_2_out_6;

  Clock clock_1 (.out(clock_1_out));
  Button CLEAR (.out(CLEAR_out));
  SevenSegmentEncoder _7_segment_encoder (
    .in_1(up_down_1_out_6), .out_2(_7_segment_encoder_out_2), .out_3(_7_segment_encoder_out_3),
    .out_4(_7_segment_encoder_out_4), .out_5(_7_segment_encoder_out_5), .out_6(_7_segment_encoder_out_6),
    .out_7(_7_segment_encoder_out_7), .out_8(_7_segment_encoder_out_8));
  SevenSegmentEncoder _7_segment_encoder_2 (
    .in_1(up_down_2_out_6), .out_2(_7_segment_encoder_2_out_2), .out_3(_7_segment_encoder_2_out_3),
    .out_4(_7_segment_encoder_2_out_4), .out_5(_7_segment_encoder_2_out_5),
    .out_6(_7_segment_encoder_2_out_6), .out_7(_7_segment_encoder_2_out_7), .out_8(_7_segment_encoder_2_out_8));
  _7_Segment_Display u_7_segment_display_1 (
    .g(_7_segment_encoder_2_out_8), .f(_7_segment_encoder_2_out_7), .a(_7_segment_encoder_2_out_2),
    .b(_7_segment_encoder_2_out_3), .e(_7_segment_encoder_2_out_6), .d(_7_segment_encoder_2_out_5),
    .c(_7_segment_encoder_2_out_4));  // open: dp
  UP_DOWN up_down_1 (
    .CONST(1'b1), .CLK(clock_1_out), .CLEAR(CLEAR_out), .UP_DOWN(UP_DOWN), .out_6(up_down_1_out_6),
    ._0(up_down_1__0), ._1(up_down_1__1), ._2(up_down_1__2), ._3(up_down_1__3));  // open: SET_TO_9
  _7_Segment_Display u_7_segment_display_2 (
    .g(_7_segment_encoder_out_8), .f(_7_segment_encoder_out_7), .a(_7_segment_encoder_out_2),
    .b(_7_segment_encoder_out_3), .e(_7_segment_encoder_out_6), .d(_7_segment_encoder_out_5),
    .c(_7_segment_encoder_out_4));  // open: dp
  and and_1 (and_1_out, up_down_1__0, not_1_out, not_2_out, up_down_1__3);
  not not_1 (not_1_out, up_down_1__1);
  not not_2 (not_2_out, up_down_1__2);
  not not_3 (not_3_out, up_down_1__0);
  not not_4 (not_4_out, up_down_1__1);
  not not_5 (not_5_out, up_down_1__2);
  not not_6 (not_6_out, up_down_1__3);
  and and_2 (and_2_out, and_1_out, not_7_out);
  not not_7 (not_7_out, UP_DOWN);
  and and_3 (and_3_out, not_3_out, not_4_out, not_5_out, not_6_out);
  xor xor_1 (xor_1_out, and_2_out, and_4_out);
  and and_4 (and_4_out, UP_DOWN, and_3_out);
  UP_DOWN up_down_2 (
    .CONST(1'b1), .CLK(xor_1_out), .CLEAR(CLEAR_out), .UP_DOWN(UP_DOWN), .out_6(up_down_2_out_6));  // open: SET_TO_9, _0, _1, _2, _3

  // Notes on the sheet:
  //   Mu In Nasif
  //   001910501036
  //   mod 100 UP/DOWN counter
endmodule

// decade-counter
module UP_DOWN (
  input  CONST,
  input  CLK,
  input  CLEAR,
  input  UP_DOWN,
  input  SET_TO_9,
  output [3:0] out_6,
  output _0,
  output _1,
  output _2,
  output _3
);

  wire A_qn, and_1_out, and_2_out, and_3_out, and_4_out, and_5_out, and_6_out, and_7_out, B_qn, C_qn, D_qn,
       multiplexer_1_out, multiplexer_2_out, multiplexer_3_out, multiplexer_4_out, multiplexer_5_out,
       multiplexer_6_out, or_1_out;

  or or_1 (or_1_out, and_4_out, and_2_out);
  J_K_Flip_Flop #(.trigger("falling")) D (
    .J(CONST), .clk(CLK), .K(CONST), .Q(_0), .Qn(D_qn), .preset(SET_TO_9), .reset(CLEAR));  // open: en
  and and_1 (and_1_out, D_qn, C_qn, B_qn);
  and and_2 (and_2_out, D_qn, _3);
  and and_3 (and_3_out, _0, A_qn);
  Multiplexer multiplexer_1 (.in0(and_3_out), .in1(or_1_out), .out(multiplexer_1_out), .sel(UP_DOWN));  // open: en
  Multiplexer multiplexer_2 (.in0(_0), .in1(D_qn), .out(multiplexer_2_out), .sel(UP_DOWN));  // open: en
  J_K_Flip_Flop #(.trigger("falling")) C (
    .J(multiplexer_1_out), .clk(CLK), .K(multiplexer_2_out), .Q(_1), .Qn(C_qn), .reset(CLEAR));  // open: preset, en
  and and_4 (and_4_out, D_qn, _2);
  and and_5 (and_5_out, _0, _1);
  Multiplexer multiplexer_3 (.in0(and_5_out), .in1(and_6_out), .out(multiplexer_3_out), .sel(UP_DOWN));  // open: en
  Multiplexer multiplexer_4 (.in0(and_5_out), .in1(and_2_out), .out(multiplexer_4_out), .sel(UP_DOWN));  // open: en
  and and_6 (and_6_out, C_qn, D_qn);
  J_K_Flip_Flop #(.trigger("falling")) B (
    .J(multiplexer_4_out), .clk(CLK), .K(multiplexer_3_out), .Q(_2), .Qn(B_qn), .reset(CLEAR));  // open: preset, en
  and and_7 (and_7_out, _0, _1, _2);
  Multiplexer multiplexer_5 (.in0(_0), .in1(D_qn), .out(multiplexer_5_out), .sel(UP_DOWN));  // open: en
  Multiplexer multiplexer_6 (.in0(and_7_out), .in1(and_1_out), .out(multiplexer_6_out), .sel(UP_DOWN));  // open: en
  J_K_Flip_Flop #(.trigger("falling")) A (
    .J(multiplexer_6_out), .clk(CLK), .K(multiplexer_5_out), .Q(_3), .Qn(A_qn), .preset(SET_TO_9),
    .reset(CLEAR));  // open: en

  assign out_6 = {_3, _2, _1, _0};
endmodule

module SevenSegmentEncoder (
  input  [3:0] in_1,
  output out_2,
  output out_3,
  output out_4,
  output out_5,
  output out_6,
  output out_7,
  output out_8
);

  wire and_1_out, B_prime_C_out, B_prime_D_prime_out, BC_prime_D_out, BC_prime_out, BD_out,
       C_prime_D_prime_out, CD_out, CD_prime_2_out, CD_prime_out, not_1_out, not_2_out, not_3_out, not_4_out;

  not not_1 (not_1_out, in_1[0]);
  not not_2 (not_2_out, in_1[1]);
  not not_3 (not_3_out, in_1[2]);
  not not_4 (not_4_out, in_1[3]);
  and BD (BD_out, in_1[0], in_1[2]);
  and B_prime_D_prime (B_prime_D_prime_out, not_1_out, not_3_out);
  and C_prime_D_prime (C_prime_D_prime_out, not_2_out, not_1_out);
  and CD (CD_out, in_1[1], in_1[0]);
  or or_1 (out_4, in_1[2], not_2_out, in_1[0]);
  and BC_prime_D (BC_prime_D_out, in_1[2], not_2_out, in_1[0]);
  and B_prime_C (B_prime_C_out, not_3_out, in_1[1]);
  and CD_prime (CD_prime_out, in_1[1], not_1_out);
  and BC_prime (BC_prime_out, in_1[2], not_2_out);
  and and_1 (and_1_out, in_1[2], not_1_out);
  or or_2 (out_2, B_prime_D_prime_out, BD_out, in_1[3], in_1[1]);
  or or_3 (out_3, not_3_out, C_prime_D_prime_out, CD_out);
  and CD_prime_2 (CD_prime_2_out, not_1_out, in_1[1]);
  or or_4 (out_6, B_prime_D_prime_out, CD_prime_out);
  or or_5 (out_7, in_1[3], C_prime_D_prime_out, BC_prime_out, and_1_out);
  or or_6 (out_8, BC_prime_out, CD_prime_out, B_prime_C_out, in_1[3]);
  or or_7 (out_5, B_prime_D_prime_out, CD_prime_2_out, BC_prime_D_out, B_prime_C_out, in_1[3]);

  // Notes on the sheet:
  //   D'
  //   C'
  //   B'
  //   A'
endmodule
