// Logisim project COUNTER.circ as structural Verilog: 1 circuit, main circuit main
module main (
  input  in_1,
  input  BUTTON,
  output B8,
  output B4,
  output B2,
  output B1
);

  wire j_k_ff_1_qn, j_k_ff_2_qn, j_k_ff_3_qn;

  J_K_Flip_Flop j_k_ff_1 (.J(in_1), .clk(BUTTON), .K(in_1), .Q(B8), .Qn(j_k_ff_1_qn));  // open: preset, en, reset
  J_K_Flip_Flop j_k_ff_2 (.J(in_1), .clk(j_k_ff_1_qn), .K(in_1), .Q(B4), .Qn(j_k_ff_2_qn));  // open: preset, en, reset
  J_K_Flip_Flop j_k_ff_3 (.J(in_1), .clk(j_k_ff_2_qn), .K(in_1), .Q(B2), .Qn(j_k_ff_3_qn));  // open: preset, en, reset
  J_K_Flip_Flop j_k_ff_4 (.J(in_1), .clk(j_k_ff_3_qn), .K(in_1), .Q(B1));  // open: Qn, preset, en, reset
endmodule
