// Logisim project Decade_Counter.circ as structural Verilog: 1 circuit, main circuit main
module main (
  input  in_1,
  input  in_2,
  input  CLEAR,
  input  UP_DOWN,
  output [3:0] out_5
);

  wire and_1_out, and_2_out, and_3_out, and_4_out, and_5_out, and_6_out, and_7_out, and_8_out, and_9_out,
       and_10_out, and_11_out, j_k_ff_1_qn, j_k_ff_2_qn, j_k_ff_3_qn, j_k_ff_4_qn, multiplexer_1_out,
       multiplexer_2_out, multiplexer_3_out, or_1_out, or_2_out, or_3_out;

  and and_1 (and_1_out, j_k_ff_4_qn, out_5[0]);
  J_K_Flip_Flop #(.trigger("falling")) j_k_ff_1 (
    .J(in_1), .clk(in_2), .K(in_1), .Q(out_5[0]), .Qn(j_k_ff_1_qn), .reset(CLEAR));  // open: preset, en
  and and_2 (and_2_out, j_k_ff_1_qn, out_5[1]);
  and and_3 (and_3_out, out_5[2], j_k_ff_1_qn);
  and and_4 (and_4_out, j_k_ff_1_qn, out_5[3]);
  Multiplexer #(.enable("false")) multiplexer_1 (
    .in0(and_1_out), .in1(or_1_out), .out(multiplexer_1_out), .sel(UP_DOWN));
  or or_1 (or_1_out, and_2_out, and_3_out, and_4_out);
  J_K_Flip_Flop #(.trigger("falling")) j_k_ff_2 (
    .J(multiplexer_1_out), .clk(in_2), .K(multiplexer_1_out), .Q(out_5[1]), .Qn(j_k_ff_2_qn), .reset(CLEAR));  // open: preset, en
  and and_5 (and_5_out, out_5[0], out_5[1]);
  and and_6 (and_6_out, j_k_ff_1_qn, j_k_ff_2_qn);
  and and_7 (and_7_out, out_5[2], and_6_out);
  and and_8 (and_8_out, and_6_out, out_5[3]);
  and and_9 (and_9_out, and_5_out, out_5[2]);
  Multiplexer #(.enable("false")) multiplexer_2 (
    .in0(and_5_out), .in1(or_2_out), .out(multiplexer_2_out), .sel(UP_DOWN));
  or or_2 (or_2_out, and_7_out, and_8_out);
  J_K_Flip_Flop #(.trigger("falling")) j_k_ff_3 (
    .J(multiplexer_2_out), .clk(in_2), .K(multiplexer_2_out), .Q(out_5[2]), .Qn(j_k_ff_3_qn), .reset(CLEAR));  // open: preset, en
  and and_10 (and_10_out, out_5[0], out_5[3]);
  and and_11 (and_11_out, j_k_ff_3_qn, j_k_ff_2_qn, j_k_ff_1_qn);
  or or_3 (or_3_out, and_10_out, and_9_out);
  Multiplexer #(.enable("false")) multiplexer_3 (
    .in0(or_3_out), .in1(and_11_out), .out(multiplexer_3_out), .sel(UP_DOWN));
  J_K_Flip_Flop #(.trigger("falling")) j_k_ff_4 (
    .J(multiplexer_3_out), .clk(in_2), .K(multiplexer_3_out), .Q(out_5[3]), .Qn(j_k_ff_4_qn), .reset(CLEAR));  // open: preset, en
endmodule
