// Logisim project Decade_up_down_with_7segment.circ as structural Verilog: 3 circuits, main circuit main
module main (
  input  _1_FOR_DOWN_0_FOR_UP
);

  wire _7_SEGMENT_ENCODER_out_2, _7_SEGMENT_ENCODER_out_3, _7_SEGMENT_ENCODER_out_4,
       _7_SEGMENT_ENCODER_out_5, _7_SEGMENT_ENCODER_out_6, _7_SEGMENT_ENCODER_out_7,
       _7_SEGMENT_ENCODER_out_8, CLEAR_out;
  wire [3:0] DECADE_UP_DOWN_COUNTER_out_3;

  Button CLEAR (.out(CLEAR_out));
  DECADE_UP_DOWN_COUNTER DECADE_UP_DOWN_COUNTER (
    .CLEAR(CLEAR_out), .UP_DOWN(_1_FOR_DOWN_0_FOR_UP), .out_3(DECADE_UP_DOWN_COUNTER_out_3));
  _7_segment_encoder _7_SEGMENT_ENCODER (
    .in_1(DECADE_UP_DOWN_COUNTER_out_3), .out_2(_7_SEGMENT_ENCODER_out_2), .out_3(_7_SEGMENT_ENCODER_out_3),
    .out_4(_7_SEGMENT_ENCODER_out_4), .out_5(_7_SEGMENT_ENCODER_out_5), .out_6(_7_SEGMENT_ENCODER_out_6),
    .out_7(_7_SEGMENT_ENCODER_out_7), .out_8(_7_SEGMENT_ENCODER_out_8));
  _7_Segment_Display u_7_segment_display_1 (
    .g(_7_SEGMENT_ENCODER_out_8), .f(_7_SEGMENT_ENCODER_out_7), .a(_7_SEGMENT_ENCODER_out_2),
    .b(_7_SEGMENT_ENCODER_out_3), .e(_7_SEGMENT_ENCODER_out_6), .d(_7_SEGMENT_ENCODER_out_5),
    .c(_7_SEGMENT_ENCODER_out_4));  // open: dp
endmodule

module _7_segment_encoder (
  input  [3:0] in_1,
  output out_2,
  output out_3,
  output out_4,
  output out_5,
  output out_6,
  output out_7,
  output out_8
);

  wire and_1_out, B_prime_C_out, B_prime_D_prime_out, BC_prime_D_out, BC_prime_out, BD_out,
       C_prime_D_prime_out, CD_out, CD_prime_2_out, CD_prime_out, not_1_out, not_2_out, not_3_out;

  not not_1 (not_1_out, in_1[0]);
  not not_2 (not_2_out, in_1[1]);
  not not_3 (not_3_out, in_1[2]);
  and BD (BD_out, in_1[0], in_1[2]);
  and B_prime_D_prime (B_prime_D_prime_out, not_1_out, not_3_out);
  and C_prime_D_prime (C_prime_D_prime_out, not_2_out, not_1_out);
  and CD (CD_out, in_1[1], in_1[0]);
  or or_1 (out_4, in_1[2], not_2_out, in_1[0]);
  and BC_prime_D (BC_prime_D_out, in_1[2], not_2_out, in_1[0]);
  and B_prime_C (B_prime_C_out, not_3_out, in_1[1]);
  and CD_prime (CD_prime_out, in_1[1], not_1_out);
  and BC_prime (BC_prime_out, in_1[2], not_2_out);
  and and_1 (and_1_out, in_1[2], not_1_out);
  or or_2 (out_2, B_prime_D_prime_out, BD_out, in_1[3], in_1[1]);
  or or_3 (out_3, not_3_out, C_prime_D_prime_out, CD_out);
  and CD_prime_2 (CD_prime_2_out, not_1_out, in_1[1]);
  or or_4 (out_6, B_prime_D_prime_out, CD_prime_out);
  or or_5 (out_7, in_1[3], C_prime_D_prime_out, BC_prime_out, and_1_out);
  or or_6 (out_8, BC_prime_out, CD_prime_out, B_prime_C_out, in_1[3]);
  or or_7 (out_5, B_prime_D_prime_out, CD_prime_2_out, BC_prime_D_out, B_prime_C_out, in_1[3]);

  // Notes on the sheet:
  //   D'
  //   C'
  //   B'
  //   A'
endmodule

module DECADE_UP_DOWN_COUNTER (
  input  CLEAR,
  input  UP_DOWN,
  output [3:0] out_3
);

  wire and_1_out, and_2_out, and_3_out, and_4_out, and_5_out, and_6_out, and_7_out, and_8_out, and_9_out,
       and_10_out, and_11_out, clock_1_out, j_k_ff_1_qn, j_k_ff_2_qn, j_k_ff_3_qn, j_k_ff_4_qn,
       multiplexer_1_out, multiplexer_2_out, multiplexer_3_out, or_1_out, or_2_out, or_3_out;

  Clock clock_1 (.out(clock_1_out));
  and and_1 (and_1_out, j_k_ff_4_qn, out_3[0]);
  J_K_Flip_Flop j_k_ff_1 (
    .J(1'b1), .clk(clock_1_out), .K(1'b1), .Q(out_3[0]), .Qn(j_k_ff_1_qn), .reset(CLEAR));  // open: preset, en
  and and_2 (and_2_out, j_k_ff_1_qn, out_3[1]);
  and and_3 (and_3_out, out_3[2], j_k_ff_1_qn);
  and and_4 (and_4_out, j_k_ff_1_qn, out_3[3]);
  Multiplexer #(.enable("false")) multiplexer_1 (
    .in0(and_1_out), .in1(or_1_out), .out(multiplexer_1_out), .sel(UP_DOWN));
  or or_1 (or_1_out, and_2_out, and_3_out, and_4_out);
  J_K_Flip_Flop j_k_ff_2 (
    .J(multiplexer_1_out), .clk(clock_1_out), .K(multiplexer_1_out), .Q(out_3[1]), .Qn(j_k_ff_2_qn),
    .reset(CLEAR));  // open: preset, en
  and and_5 (and_5_out, out_3[0], out_3[1]);
  and and_6 (and_6_out, j_k_ff_1_qn, j_k_ff_2_qn);
  and and_7 (and_7_out, out_3[2], and_6_out);
  and and_8 (and_8_out, and_6_out, out_3[3]);
  and and_9 (and_9_out, and_5_out, out_3[2]);
  Multiplexer #(.enable("false")) multiplexer_2 (
    .in0(and_5_out), .in1(or_2_out), .out(multiplexer_2_out), .sel(UP_DOWN));
  or or_2 (or_2_out, and_7_out, and_8_out);
  J_K_Flip_Flop j_k_ff_3 (
    .J(multiplexer_2_out), .clk(clock_1_out), .K(multiplexer_2_out), .Q(out_3[2]), .Qn(j_k_ff_3_qn),
    .reset(CLEAR));  // open: preset, en
  and and_10 (and_10_out, out_3[0], out_3[3]);
  and and_11 (and_11_out, j_k_ff_3_qn, j_k_ff_2_qn, j_k_ff_1_qn);
  or or_3 (or_3_out, and_10_out, and_9_out);
  Multiplexer #(.enable("false")) multiplexer_3 (
    .in0(or_3_out), .in1(and_11_out), .out(multiplexer_3_out), .sel(UP_DOWN));
  J_K_Flip_Flop j_k_ff_4 (
    .J(multiplexer_3_out), .clk(clock_1_out), .K(multiplexer_3_out), .Q(out_3[3]), .Qn(j_k_ff_4_qn),
    .reset(CLEAR));  // open: preset, en
endmodule
