// Logisim project MOD24.circ as structural Verilog: 1 circuit, main circuit main
module main (
  input  CLK,
  input  CLR,
  output [3:0] _2,
  output [3:0] _4
);

  wire and_1_out, and_2_out, and_3_out, and_4_out, and_5_out, main_1__0, main_1__1, main_1__2, main_1__3,
       not_1_out, not_2_out, not_3_out, not_4_out, not_5_out, or_1_out;

  or or_1 (or_1_out, CLR, and_1_out);
  Hex_Digit_Display hex_digit_display_1 (.value(_2));  // open: dp
  Up_Down_final_main main_1 (
    .CONST(1'b1), .CLK(CLK), .CLEAR(or_1_out), .UP_DOWN(1'b0), .out_6(_4), ._0(main_1__0), ._1(main_1__1),
    ._2(main_1__2), ._3(main_1__3));  // open: SET_TO_9
  and and_1 (and_1_out, CLK, and_4_out, and_5_out);
  Hex_Digit_Display hex_digit_display_2 (.value(_4));  // open: dp
  not not_1 (not_1_out, main_1__1);
  not not_2 (not_2_out, main_1__2);
  and and_2 (and_2_out, and_3_out, CLK);
  and and_3 (and_3_out, main_1__0, not_1_out, not_2_out, main_1__3);
  not not_3 (not_3_out, main_1__3);
  not not_4 (not_4_out, main_1__2);
  and and_4 (and_4_out, not_3_out, not_4_out, main_1__1, main_1__0);
  MOD2_COUNTER_main main_2 (.CLK(and_2_out), .CLEAR(or_1_out), ._2(_2));
  and and_5 (and_5_out, _2[1], not_5_out);
  not not_5 (not_5_out, _2[0]);
endmodule
