// Logisim project MOD2_COUNTER.circ as structural Verilog: 1 circuit, main circuit main
module main (
  input  CLK,
  input  CLEAR,
  output [3:0] _2
);

  wire A_qn;

  J_K_Flip_Flop B (.J(A_qn), .clk(CLK), .K(1'b1), .Q(_2[0]), .reset(CLEAR));  // open: Qn, preset, en
  J_K_Flip_Flop A (.J(_2[0]), .clk(CLK), .K(1'b1), .Q(_2[1]), .Qn(A_qn), .reset(CLEAR));  // open: preset, en

  assign _2[3:2] = 2'b00;
endmodule
