// Logisim project MOD4.circ as structural Verilog: 1 circuit, main circuit main
module main (
  input  CLK,
  input  CLEAR,
  output [3:0] _3
);

  wire C_qn;

  J_K_Flip_Flop C (.J(1'b1), .clk(CLK), .K(1'b1), .Q(_3[0]), .Qn(C_qn), .reset(CLEAR));  // open: preset, en
  J_K_Flip_Flop B (.J(1'b1), .clk(C_qn), .K(1'b1), .Q(_3[1]), .reset(CLEAR));  // open: Qn, preset, en
  Hex_Digit_Display hex_digit_display_1 (.value({2'b00, _3[1:0]}));  // open: dp

  assign _3[3:2] = 2'b00;
endmodule
