// Logisim project Mod-60-counter.circ as structural Verilog: 4 circuits, main circuit main
module main (
  input  up_down_not_ready
);

  wire and_1_out, and_2_out, and_3_out, and_4_out, clear_out, clk_out, mod_10_counter__0, mod_10_counter__1,
       mod_10_counter__2, mod_10_counter__3, not_1_out, not_2_out, not_3_out, or_1_out,
       sevensegmentencoder_1_out_2, sevensegmentencoder_1_out_3, sevensegmentencoder_1_out_4,
       sevensegmentencoder_1_out_5, sevensegmentencoder_1_out_6, sevensegmentencoder_1_out_7,
       sevensegmentencoder_1_out_8, sevensegmentencoder_2_out_2, sevensegmentencoder_2_out_3,
       sevensegmentencoder_2_out_4, sevensegmentencoder_2_out_5, sevensegmentencoder_2_out_6,
       sevensegmentencoder_2_out_7, sevensegmentencoder_2_out_8;
  wire [2:0] mod_6_counter_out_4;
  wire [3:0] mod_10_counter_out_6;

  Clock clk (.out(clk_out));
  Button clear (.out(clear_out));
  SevenSegmentEncoder sevensegmentencoder_1 (
    .in_1({1'b0, mod_6_counter_out_4}), .out_2(sevensegmentencoder_1_out_2),
    .out_3(sevensegmentencoder_1_out_3), .out_4(sevensegmentencoder_1_out_4),
    .out_5(sevensegmentencoder_1_out_5), .out_6(sevensegmentencoder_1_out_6),
    .out_7(sevensegmentencoder_1_out_7), .out_8(sevensegmentencoder_1_out_8));
  or or_1 (or_1_out, clear_out, and_3_out);
  _7_Segment_Display u_7_segment_display_1 (
    .g(sevensegmentencoder_2_out_8), .f(sevensegmentencoder_2_out_7), .a(sevensegmentencoder_2_out_2),
    .b(sevensegmentencoder_2_out_3), .e(sevensegmentencoder_2_out_6), .d(sevensegmentencoder_2_out_5),
    .c(sevensegmentencoder_2_out_4));  // open: dp
  _7_Segment_Display u_7_segment_display_2 (
    .g(sevensegmentencoder_1_out_8), .f(sevensegmentencoder_1_out_7), .a(sevensegmentencoder_1_out_2),
    .b(sevensegmentencoder_1_out_3), .e(sevensegmentencoder_1_out_6), .d(sevensegmentencoder_1_out_5),
    .c(sevensegmentencoder_1_out_4));  // open: dp
  and and_1 (and_1_out, or_1_out, clk_out);
  up_down_decade mod_10_counter (
    .CONST(1'b1), .CLK(clk_out), .CLEAR(and_1_out), .UP_DOWN(up_down_not_ready),
    .out_6(mod_10_counter_out_6), ._0(mod_10_counter__0), ._1(mod_10_counter__1), ._2(mod_10_counter__2),
    ._3(mod_10_counter__3));  // open: SET_TO_9
  not not_1 (not_1_out, mod_10_counter__1);
  not not_2 (not_2_out, mod_10_counter__2);
  and and_2 (and_2_out, mod_10_counter__3, not_2_out, not_1_out, mod_10_counter__0);
  SevenSegmentEncoder sevensegmentencoder_2 (
    .in_1(mod_10_counter_out_6), .out_2(sevensegmentencoder_2_out_2), .out_3(sevensegmentencoder_2_out_3),
    .out_4(sevensegmentencoder_2_out_4), .out_5(sevensegmentencoder_2_out_5),
    .out_6(sevensegmentencoder_2_out_6), .out_7(sevensegmentencoder_2_out_7),
    .out_8(sevensegmentencoder_2_out_8));
  and and_3 (and_3_out, and_2_out, and_4_out);
  mod6_up mod_6_counter (.CONST(1'b1), .CLK(and_2_out), .CLEAR(and_1_out), .out_4(mod_6_counter_out_4));
  not not_3 (not_3_out, mod_6_counter_out_4[1]);
  and and_4 (and_4_out, mod_6_counter_out_4[2], not_3_out, mod_6_counter_out_4[0]);
endmodule

module up_down_decade (
  input  CONST,
  input  CLK,
  input  CLEAR,
  input  UP_DOWN,
  input  SET_TO_9,
  output [3:0] out_6,
  output _0,
  output _1,
  output _2,
  output _3
);

  wire A_qn, and_1_out, and_2_out, and_3_out, and_4_out, and_5_out, and_6_out, and_7_out, B_qn, C_qn, D_qn,
       multiplexer_1_out, multiplexer_2_out, multiplexer_3_out, multiplexer_4_out, multiplexer_5_out,
       multiplexer_6_out, or_1_out;

  or or_1 (or_1_out, and_4_out, and_2_out);
  J_K_Flip_Flop #(.trigger("falling")) D (
    .J(CONST), .clk(CLK), .K(CONST), .Q(_0), .Qn(D_qn), .preset(SET_TO_9), .reset(CLEAR));  // open: en
  and and_1 (and_1_out, D_qn, C_qn, B_qn);
  and and_2 (and_2_out, D_qn, _3);
  and and_3 (and_3_out, _0, A_qn);
  Multiplexer multiplexer_1 (.in0(and_3_out), .in1(or_1_out), .out(multiplexer_1_out), .sel(UP_DOWN));  // open: en
  Multiplexer multiplexer_2 (.in0(_0), .in1(D_qn), .out(multiplexer_2_out), .sel(UP_DOWN));  // open: en
  J_K_Flip_Flop #(.trigger("falling")) C (
    .J(multiplexer_1_out), .clk(CLK), .K(multiplexer_2_out), .Q(_1), .Qn(C_qn), .reset(CLEAR));  // open: preset, en
  and and_4 (and_4_out, D_qn, _2);
  and and_5 (and_5_out, _0, _1);
  Multiplexer multiplexer_3 (.in0(and_5_out), .in1(and_6_out), .out(multiplexer_3_out), .sel(UP_DOWN));  // open: en
  Multiplexer multiplexer_4 (.in0(and_5_out), .in1(and_2_out), .out(multiplexer_4_out), .sel(UP_DOWN));  // open: en
  and and_6 (and_6_out, C_qn, D_qn);
  J_K_Flip_Flop #(.trigger("falling")) B (
    .J(multiplexer_4_out), .clk(CLK), .K(multiplexer_3_out), .Q(_2), .Qn(B_qn), .reset(CLEAR));  // open: preset, en
  and and_7 (and_7_out, _0, _1, _2);
  Multiplexer multiplexer_5 (.in0(_0), .in1(D_qn), .out(multiplexer_5_out), .sel(UP_DOWN));  // open: en
  Multiplexer multiplexer_6 (.in0(and_7_out), .in1(and_1_out), .out(multiplexer_6_out), .sel(UP_DOWN));  // open: en
  J_K_Flip_Flop #(.trigger("falling")) A (
    .J(multiplexer_6_out), .clk(CLK), .K(multiplexer_5_out), .Q(_3), .Qn(A_qn), .preset(SET_TO_9),
    .reset(CLEAR));  // open: en

  assign out_6 = {_3, _2, _1, _0};
endmodule

module mod6_up (
  input  CONST,
  input  CLK,
  input  CLEAR,
  output [2:0] out_4
);

  wire A_qn, and_1_out, and_2_out;

  J_K_Flip_Flop #(.trigger("falling")) C (
    .J(CONST), .clk(CLK), .K(CONST), .Q(out_4[0]), .reset(CLEAR));  // open: Qn, preset, en
  J_K_Flip_Flop #(.trigger("falling")) B (
    .J(and_1_out), .clk(CLK), .K(out_4[0]), .Q(out_4[1]), .reset(CLEAR));  // open: Qn, preset, en
  and and_1 (and_1_out, out_4[0], A_qn);
  and and_2 (and_2_out, out_4[1], out_4[0]);
  J_K_Flip_Flop #(.trigger("falling")) A (
    .J(and_2_out), .clk(CLK), .K(out_4[0]), .Q(out_4[2]), .Qn(A_qn), .reset(CLEAR));  // open: preset, en
endmodule

module SevenSegmentEncoder (
  input  [3:0] in_1,
  output out_2,
  output out_3,
  output out_4,
  output out_5,
  output out_6,
  output out_7,
  output out_8
);

  wire and_1_out, B_prime_C_out, B_prime_D_prime_out, BC_prime_D_out, BC_prime_out, BD_out,
       C_prime_D_prime_out, CD_out, CD_prime_2_out, CD_prime_out, not_1_out, not_2_out, not_3_out, not_4_out;

  and BD (BD_out, in_1[0], in_1[2]);
  not not_1 (not_1_out, in_1[0]);
  not not_2 (not_2_out, in_1[1]);
  not not_3 (not_3_out, in_1[2]);
  not not_4 (not_4_out, in_1[3]);
  and B_prime_D_prime (B_prime_D_prime_out, not_1_out, not_3_out);
  and C_prime_D_prime (C_prime_D_prime_out, not_2_out, not_1_out);
  and CD (CD_out, in_1[1], in_1[0]);
  or or_1 (out_4, in_1[2], not_2_out, in_1[0]);
  and BC_prime_D (BC_prime_D_out, in_1[2], not_2_out, in_1[0]);
  and B_prime_C (B_prime_C_out, not_3_out, in_1[1]);
  and CD_prime (CD_prime_out, in_1[1], not_1_out);
  and BC_prime (BC_prime_out, in_1[2], not_2_out);
  and and_1 (and_1_out, in_1[2], not_1_out);
  or or_2 (out_2, B_prime_D_prime_out, BD_out, in_1[3], in_1[1]);
  or or_3 (out_3, not_3_out, C_prime_D_prime_out, CD_out);
  and CD_prime_2 (CD_prime_2_out, not_1_out, in_1[1]);
  or or_4 (out_5, B_prime_D_prime_out, CD_prime_2_out, BC_prime_D_out, B_prime_C_out, in_1[3]);
  or or_5 (out_6, B_prime_D_prime_out, CD_prime_out);
  or or_6 (out_7, in_1[3], C_prime_D_prime_out, BC_prime_out, and_1_out);
  or or_7 (out_8, BC_prime_out, CD_prime_out, B_prime_C_out, in_1[3]);

  // Notes on the sheet:
  //   D'
  //   C'
  //   B'
  //   A'
endmodule
