// Logisim project SEVEN_SEGMENT_LED_WITH_DECODER.circ as structural Verilog: 1 circuit, main circuit main
module main (
  input  ON_OFF,
  output [3:0] out_2
);

  wire button_1_out, SEVEN_SEGMENT_DECODER_p2, SEVEN_SEGMENT_DECODER_p3, SEVEN_SEGMENT_DECODER_p4,
       SEVEN_SEGMENT_DECODER_p5, SEVEN_SEGMENT_DECODER_p6, SEVEN_SEGMENT_DECODER_p7, SEVEN_SEGMENT_DECODER_p8;

  Button button_1 (.out(button_1_out));
  COUNTER_main main_1 (
    .BUTTON(button_1_out), .in_1(ON_OFF), .B8(out_2[0]), .B4(out_2[1]), .B2(out_2[2]), .B1(out_2[3]));
  // SEVENdECODER_main SEVEN_SEGMENT_DECODER: pin names not known; wires that end beside it: out_2, SEVEN_SEGMENT_DECODER_p2, SEVEN_SEGMENT_DECODER_p3, SEVEN_SEGMENT_DECODER_p4, SEVEN_SEGMENT_DECODER_p5, SEVEN_SEGMENT_DECODER_p6, SEVEN_SEGMENT_DECODER_p7, SEVEN_SEGMENT_DECODER_p8
  _7_Segment_Display u_7_segment_display_1 (
    .g(SEVEN_SEGMENT_DECODER_p8), .f(SEVEN_SEGMENT_DECODER_p7), .a(SEVEN_SEGMENT_DECODER_p2),
    .b(SEVEN_SEGMENT_DECODER_p3), .e(SEVEN_SEGMENT_DECODER_p6), .d(SEVEN_SEGMENT_DECODER_p5),
    .c(SEVEN_SEGMENT_DECODER_p4));  // open: dp
endmodule
