// Logisim project SEVEN_SEGMENT_LED_WITH_ENDCODER.circ as structural Verilog: 3 circuits, main circuit main
module main (
  input  ON_OFF,
  output [3:0] out_2
);

  wire button_1_out, Seven_Segment_Encoder_out_2, Seven_Segment_Encoder_out_3, Seven_Segment_Encoder_out_4,
       Seven_Segment_Encoder_out_5, Seven_Segment_Encoder_out_6, Seven_Segment_Encoder_out_7,
       Seven_Segment_Encoder_out_8;

  Button button_1 (.out(button_1_out));
  Counter counter_4_bit (
    .BUTTON(button_1_out), .in_1(ON_OFF), .B8(out_2[0]), .B4(out_2[1]), .B2(out_2[2]), .B1(out_2[3]));
  _7_SegmentEncoder Seven_Segment_Encoder (
    .in_1(out_2), .out_2(Seven_Segment_Encoder_out_2), .out_3(Seven_Segment_Encoder_out_3),
    .out_4(Seven_Segment_Encoder_out_4), .out_5(Seven_Segment_Encoder_out_5),
    .out_6(Seven_Segment_Encoder_out_6), .out_7(Seven_Segment_Encoder_out_7),
    .out_8(Seven_Segment_Encoder_out_8));
  _7_Segment_Display u_7_segment_display_1 (
    .g(Seven_Segment_Encoder_out_8), .f(Seven_Segment_Encoder_out_7), .a(Seven_Segment_Encoder_out_2),
    .b(Seven_Segment_Encoder_out_3), .e(Seven_Segment_Encoder_out_6), .d(Seven_Segment_Encoder_out_5),
    .c(Seven_Segment_Encoder_out_4));  // open: dp
endmodule

module _7_SegmentEncoder (
  input  [3:0] in_1,
  output out_2,
  output out_3,
  output out_4,
  output out_5,
  output out_6,
  output out_7,
  output out_8
);

  wire and_1_out, B_prime_C_out, B_prime_D_prime_out, BC_prime_D_out, BC_prime_out, BD_out,
       C_prime_D_prime_out, CD_out, CD_prime_2_out, CD_prime_out, not_1_out, not_2_out, not_3_out, not_4_out;

  not not_1 (not_1_out, in_1[0]);
  not not_2 (not_2_out, in_1[1]);
  not not_3 (not_3_out, in_1[2]);
  not not_4 (not_4_out, in_1[3]);
  and BD (BD_out, in_1[0], in_1[2]);
  and B_prime_D_prime (B_prime_D_prime_out, not_1_out, not_3_out);
  and C_prime_D_prime (C_prime_D_prime_out, not_2_out, not_1_out);
  and CD (CD_out, in_1[1], in_1[0]);
  or or_1 (out_4, in_1[2], not_2_out, in_1[0]);
  and BC_prime_D (BC_prime_D_out, in_1[2], not_2_out, in_1[0]);
  and B_prime_C (B_prime_C_out, not_3_out, in_1[1]);
  and CD_prime (CD_prime_out, in_1[1], not_1_out);
  and BC_prime (BC_prime_out, in_1[2], not_2_out);
  and and_1 (and_1_out, in_1[2], not_1_out);
  or or_2 (out_2, B_prime_D_prime_out, BD_out, in_1[3], in_1[1]);
  or or_3 (out_3, not_3_out, C_prime_D_prime_out, CD_out);
  and CD_prime_2 (CD_prime_2_out, not_1_out, in_1[1]);
  or or_4 (out_6, B_prime_D_prime_out, CD_prime_out);
  or or_5 (out_7, in_1[3], C_prime_D_prime_out, BC_prime_out, and_1_out);
  or or_6 (out_8, BC_prime_out, CD_prime_out, B_prime_C_out, in_1[3]);
  or or_7 (out_5, B_prime_D_prime_out, CD_prime_2_out, BC_prime_D_out, B_prime_C_out, in_1[3]);

  // Notes on the sheet:
  //   D'
  //   C'
  //   B'
  //   A'
endmodule

module Counter (
  input  in_1,
  input  BUTTON,
  output B8,
  output B4,
  output B2,
  output B1
);

  wire j_k_ff_1_qn, j_k_ff_2_qn, j_k_ff_3_qn;

  J_K_Flip_Flop j_k_ff_1 (.J(in_1), .clk(BUTTON), .K(in_1), .Q(B8), .Qn(j_k_ff_1_qn));  // open: preset, en, reset
  J_K_Flip_Flop j_k_ff_2 (.J(in_1), .clk(j_k_ff_1_qn), .K(in_1), .Q(B4), .Qn(j_k_ff_2_qn));  // open: preset, en, reset
  J_K_Flip_Flop j_k_ff_3 (.J(in_1), .clk(j_k_ff_2_qn), .K(in_1), .Q(B2), .Qn(j_k_ff_3_qn));  // open: preset, en, reset
  J_K_Flip_Flop j_k_ff_4 (.J(in_1), .clk(j_k_ff_3_qn), .K(in_1), .Q(B1));  // open: Qn, preset, en, reset
endmodule
