// Logisim project SevenSegmentEncoder.circ as structural Verilog: 1 circuit, main circuit main
module main (
  input  [3:0] in_1,
  output out_2,
  output out_3,
  output out_4,
  output out_5,
  output out_6,
  output out_7,
  output out_8
);

  wire and_1_out, B_prime_C_out, B_prime_D_prime_out, BC_prime_D_out, BC_prime_out, BD_out,
       C_prime_D_prime_out, CD_out, CD_prime_2_out, CD_prime_out, not_1_out, not_2_out, not_3_out, not_4_out;

  and BD (BD_out, in_1[0], in_1[2]);
  not not_1 (not_1_out, in_1[0]);
  not not_2 (not_2_out, in_1[1]);
  not not_3 (not_3_out, in_1[2]);
  not not_4 (not_4_out, in_1[3]);
  and B_prime_D_prime (B_prime_D_prime_out, not_1_out, not_3_out);
  and C_prime_D_prime (C_prime_D_prime_out, not_2_out, not_1_out);
  and CD (CD_out, in_1[1], in_1[0]);
  or or_1 (out_4, in_1[2], not_2_out, in_1[0]);
  and BC_prime_D (BC_prime_D_out, in_1[2], not_2_out, in_1[0]);
  and B_prime_C (B_prime_C_out, not_3_out, in_1[1]);
  and CD_prime (CD_prime_out, in_1[1], not_1_out);
  and BC_prime (BC_prime_out, in_1[2], not_2_out);
  and and_1 (and_1_out, in_1[2], not_1_out);
  or or_2 (out_2, B_prime_D_prime_out, BD_out, in_1[3], in_1[1]);
  or or_3 (out_3, not_3_out, C_prime_D_prime_out, CD_out);
  and CD_prime_2 (CD_prime_2_out, not_1_out, in_1[1]);
  or or_4 (out_5, B_prime_D_prime_out, CD_prime_2_out, BC_prime_D_out, B_prime_C_out, in_1[3]);
  or or_5 (out_6, B_prime_D_prime_out, CD_prime_out);
  or or_6 (out_7, in_1[3], C_prime_D_prime_out, BC_prime_out, and_1_out);
  or or_7 (out_8, BC_prime_out, CD_prime_out, B_prime_C_out, in_1[3]);

  // Notes on the sheet:
  //   D'
  //   C'
  //   B'
  //   A'
endmodule
