// Logisim project UP-DOWN.circ as structural Verilog: 1 circuit, main circuit main
module main (
  input  in_1,
  output [3:0] out_2
);

  wire and_2_out, and_3_out, and_4_out, clock_1_out, j_k_ff_1_qn, j_k_ff_2_qn, j_k_ff_3_qn,
       multiplexer_1_out, multiplexer_2_out, multiplexer_3_out, multiplexer_4_out, multiplexer_5_out,
       multiplexer_6_out, undriven;

  Clock clock_1 (.out(clock_1_out));
  J_K_Flip_Flop #(.trigger("falling")) j_k_ff_1 (
    .J(1'b1), .clk(clock_1_out), .K(1'b1), .Q(out_2[0]), .Qn(j_k_ff_1_qn), .reset(undriven));  // open: preset, en
  Multiplexer multiplexer_1 (.in0(clock_1_out), .in1(out_2[0]), .out(multiplexer_1_out), .sel(in_1));  // open: en
  Multiplexer multiplexer_2 (.in0(j_k_ff_1_qn), .in1(1'b1), .out(multiplexer_2_out), .sel(in_1));  // open: en
  // AND_Gate and_1 has open pins: in0=in_1, in1=and_2_out, out=open
  J_K_Flip_Flop #(.trigger("falling")) j_k_ff_2 (
    .J(multiplexer_2_out), .clk(multiplexer_1_out), .K(multiplexer_2_out), .Q(out_2[1]), .Qn(j_k_ff_2_qn),
    .reset(undriven));  // open: preset, en
  and and_2 (and_2_out, out_2[1], out_2[3]);
  Multiplexer multiplexer_3 (.in0(clock_1_out), .in1(out_2[1]), .out(multiplexer_3_out), .sel(in_1));  // open: en
  and and_3 (and_3_out, j_k_ff_2_qn, multiplexer_2_out);
  Multiplexer multiplexer_4 (.in0(and_3_out), .in1(1'b1), .out(multiplexer_4_out), .sel(in_1));  // open: en
  J_K_Flip_Flop #(.trigger("falling")) j_k_ff_3 (
    .J(multiplexer_4_out), .clk(multiplexer_3_out), .K(multiplexer_4_out), .Q(out_2[2]), .Qn(j_k_ff_3_qn),
    .reset(undriven));  // open: preset, en
  and and_4 (and_4_out, j_k_ff_3_qn, multiplexer_4_out);
  Multiplexer multiplexer_5 (.in0(clock_1_out), .in1(out_2[2]), .out(multiplexer_5_out), .sel(in_1));  // open: en
  Multiplexer multiplexer_6 (.in0(and_4_out), .in1(1'b1), .out(multiplexer_6_out), .sel(in_1));  // open: en
  J_K_Flip_Flop #(.trigger("falling")) j_k_ff_4 (
    .J(multiplexer_6_out), .clk(multiplexer_5_out), .K(multiplexer_6_out), .Q(out_2[3]), .reset(undriven));  // open: Qn, preset, en
endmodule
