// Logisim project Up_Down_final.circ as structural Verilog: 1 circuit, main circuit main
module main (
  input  CONST,
  input  CLK,
  input  CLEAR,
  input  UP_DOWN,
  input  SET_TO_9,
  output [3:0] out_6,
  output _0,
  output _1,
  output _2,
  output _3
);

  wire A_qn, and_1_out, and_2_out, and_3_out, and_4_out, and_5_out, and_6_out, and_7_out, B_qn, C_qn, D_qn,
       multiplexer_1_out, multiplexer_2_out, multiplexer_3_out, multiplexer_4_out, multiplexer_5_out,
       multiplexer_6_out, or_1_out;

  or or_1 (or_1_out, and_4_out, and_2_out);
  J_K_Flip_Flop #(.trigger("falling")) D (
    .J(CONST), .clk(CLK), .K(CONST), .Q(_0), .Qn(D_qn), .preset(SET_TO_9), .reset(CLEAR));  // open: en
  and and_1 (and_1_out, D_qn, C_qn, B_qn);
  and and_2 (and_2_out, D_qn, _3);
  and and_3 (and_3_out, _0, A_qn);
  Multiplexer multiplexer_1 (.in0(and_3_out), .in1(or_1_out), .out(multiplexer_1_out), .sel(UP_DOWN));  // open: en
  Multiplexer multiplexer_2 (.in0(_0), .in1(D_qn), .out(multiplexer_2_out), .sel(UP_DOWN));  // open: en
  J_K_Flip_Flop #(.trigger("falling")) C (
    .J(multiplexer_1_out), .clk(CLK), .K(multiplexer_2_out), .Q(_1), .Qn(C_qn), .reset(CLEAR));  // open: preset, en
  and and_4 (and_4_out, D_qn, _2);
  and and_5 (and_5_out, _0, _1);
  Multiplexer multiplexer_3 (.in0(and_5_out), .in1(and_6_out), .out(multiplexer_3_out), .sel(UP_DOWN));  // open: en
  Multiplexer multiplexer_4 (.in0(and_5_out), .in1(and_2_out), .out(multiplexer_4_out), .sel(UP_DOWN));  // open: en
  and and_6 (and_6_out, C_qn, D_qn);
  J_K_Flip_Flop #(.trigger("falling")) B (
    .J(multiplexer_4_out), .clk(CLK), .K(multiplexer_3_out), .Q(_2), .Qn(B_qn), .reset(CLEAR));  // open: preset, en
  and and_7 (and_7_out, _0, _1, _2);
  Multiplexer multiplexer_5 (.in0(_0), .in1(D_qn), .out(multiplexer_5_out), .sel(UP_DOWN));  // open: en
  Multiplexer multiplexer_6 (.in0(and_7_out), .in1(and_1_out), .out(multiplexer_6_out), .sel(UP_DOWN));  // open: en
  J_K_Flip_Flop #(.trigger("falling")) A (
    .J(multiplexer_6_out), .clk(CLK), .K(multiplexer_5_out), .Q(_3), .Qn(A_qn), .preset(SET_TO_9),
    .reset(CLEAR));  // open: en

  assign out_6 = {_3, _2, _1, _0};

  // Notes on the sheet:
  //   Mu In Nasif    001910501036
  //   mod 10 UP/DOWN counter
endmodule
