// Logisim project clock24-60-60.circ as structural Verilog: 1 circuit, main circuit main
module main (
);

  wire and_1_out, and_2_out, and_3_out, CLEAR_out, CLK_out, main_1__9, not_1_out, not_2_out;
  wire [2:0] main_1__3_bit, main_2__3_bit;
  wire [3:0] main_1__4_bit, main_2__4_bit, main_3__2, main_3__4;

  Clock CLK (.out(CLK_out));
  Button CLEAR (.out(CLEAR_out));
  mod60_for_CLK_main main_1 (
    .clk(CLK_out), .\const (1'b1), .clear(CLEAR_out), ._4_bit(main_1__4_bit), ._3_bit(main_1__3_bit),
    ._9(main_1__9));
  Hex_Digit_Display hex_digit_display_1 (.value(main_3__2));  // open: dp
  Hex_Digit_Display hex_digit_display_2 ();  // open: value, dp
  Hex_Digit_Display hex_digit_display_3 (.value(main_3__4));  // open: dp
  Hex_Digit_Display hex_digit_display_4 (.value(main_2__4_bit));  // open: dp
  Hex_Digit_Display hex_digit_display_5 (.value({1'b0, main_2__3_bit}));  // open: dp
  Hex_Digit_Display hex_digit_display_6 ();  // open: value, dp
  Hex_Digit_Display hex_digit_display_7 (.value({1'b0, main_1__3_bit}));  // open: dp
  not not_1 (not_1_out, main_1__3_bit[1]);
  and and_1 (and_1_out, main_1__3_bit[0], not_1_out, main_1__3_bit[2]);
  and and_2 (and_2_out, and_1_out, CLK_out, main_1__9);
  Hex_Digit_Display hex_digit_display_8 (.value(main_1__4_bit));  // open: dp
  mod60_for_CLK_main main_2 (
    .clk(and_2_out), .\const (1'b1), .clear(CLEAR_out), ._4_bit(main_2__4_bit), ._3_bit(main_2__3_bit));  // open: _9
  MOD24_main main_3 (.CLK(and_3_out), .CLR(CLEAR_out), ._2(main_3__2), ._4(main_3__4));
  and and_3 (and_3_out, main_2__3_bit[0], not_2_out, main_2__3_bit[2]);
  not not_2 (not_2_out, main_2__3_bit[1]);
endmodule
