// Logisim project mod6.circ as structural Verilog: 1 circuit, main circuit main
module main (
  input  CONST,
  input  CLK,
  input  CLEAR,
  output [2:0] out_4
);

  wire A_qn, and_1_out, and_2_out;

  J_K_Flip_Flop #(.trigger("falling")) C (
    .J(CONST), .clk(CLK), .K(CONST), .Q(out_4[0]), .reset(CLEAR));  // open: Qn, preset, en
  J_K_Flip_Flop #(.trigger("falling")) B (
    .J(and_1_out), .clk(CLK), .K(out_4[0]), .Q(out_4[1]), .reset(CLEAR));  // open: Qn, preset, en
  and and_1 (and_1_out, out_4[0], A_qn);
  and and_2 (and_2_out, out_4[1], out_4[0]);
  J_K_Flip_Flop #(.trigger("falling")) A (
    .J(and_2_out), .clk(CLK), .K(out_4[0]), .Q(out_4[2]), .Qn(A_qn), .reset(CLEAR));  // open: preset, en
endmodule
