// Logisim project mod60_for_CLK.circ as structural Verilog: 1 circuit, main circuit main
module main (
  input  clk,
  input  \const ,
  input  clear,
  output [3:0] _4_bit,
  output [2:0] _3_bit,
  output _9
);

  wire and_2_out, not_1_out, not_2_out, up_down_decade_1__0, up_down_decade_1__1, up_down_decade_1__2,
       up_down_decade_1__3;

  up_down_decade up_down_decade_1 (
    .CONST(\const ), .CLK(clk), .CLEAR(clear), .UP_DOWN(1'b0), .out_6(_4_bit), ._0(up_down_decade_1__0),
    ._1(up_down_decade_1__1), ._2(up_down_decade_1__2), ._3(up_down_decade_1__3));  // open: SET_TO_9
  not not_1 (not_1_out, up_down_decade_1__1);
  not not_2 (not_2_out, up_down_decade_1__2);
  and and_1 (_9, up_down_decade_1__3, not_2_out, not_1_out, up_down_decade_1__0);
  and and_2 (and_2_out, _9, clk);
  Hex_Digit_Display hex_digit_display_1 (.value(_4_bit));  // open: dp
  Hex_Digit_Display hex_digit_display_2 (.value({1'b0, _3_bit}));  // open: dp
  mod6_up mod6_up_1 (.CONST(\const ), .CLK(and_2_out), .CLEAR(clear), .out_4(_3_bit));
endmodule
