// Logisim project new.circ as structural Verilog: 1 circuit, main circuit main
module main (
);

  wire A_qn, and_1_out, and_2_out, B_qn, C_qn, clock_1_out, D_qn, or_1_out;
  wire [3:0] D_q;

  Clock clock_1 (.out(clock_1_out));
  or or_1 (or_1_out, and_1_out, and_2_out);
  and and_1 (and_1_out, D_q[0], D_q[3]);
  and and_2 (and_2_out, D_q[0], D_q[1], D_q[2]);
  J_K_Flip_Flop #(.trigger("falling")) D (
    .J(1'b1), .clk(clock_1_out), .K(1'b1), .Q(D_q[0]), .Qn(D_qn));  // open: preset, en, reset
  J_K_Flip_Flop #(.trigger("falling")) C (
    .J(D_q[0]), .clk(clock_1_out), .K(D_q[0]), .Q(D_q[1]), .Qn(C_qn));  // open: preset, en, reset
  J_K_Flip_Flop #(.trigger("falling")) B (
    .J(and_1_out), .clk(clock_1_out), .K(and_1_out), .Q(D_q[2]), .Qn(B_qn));  // open: preset, en, reset
  Hex_Digit_Display hex_digit_display_1 (.value(D_q));  // open: dp
  J_K_Flip_Flop #(.trigger("falling")) A (
    .J(or_1_out), .clk(clock_1_out), .K(or_1_out), .Q(D_q[3]), .Qn(A_qn));  // open: preset, en, reset
endmodule
